# Fritzing sketch pi-pico-rtc (saved by Fritzing 0.9.6b)
breadboards: 1

parts:
  A1 = Raspberry Pi Pico H
  S1 = Momentary Switch [package=tactile-pth]
  Part1 = Adafruit PCF8523 RTC [part_number="Adafruit #3295"]

nets:
  GND: A1.GND, S1.2, Part1.GND
  N1: A1.GP4, Part1.SDA
  N2: A1.GP5, Part1.SCL
  N3: A1.RUN, S1.3
  N4: A1.3V3OUT, Part1.VCC

custom parts:
  Raspberry Pi Pico H: Raspberry Pi Pico H. Based around the RP2040 microcontroller the Pico H is a low cost microcontroller device bringing Raspberry Pi quality, cost, and easy of use to the microcontroller space.
  Adafruit PCF8523 RTC: This is a great battery-backed real time clock (RTC) that allows your microcontroller project to keep track of time even if it is reprogrammed, or if the power is lost. Perfect for datalogging, clock-building, time stamping, timers and alarms, etc. Equipped with PCF8523 RTC - it can run from 3.3V or 5V power & logic! Works great with an Arduino using our RTC library, with CircuitPython or with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
